# Fritzing sketch gpio_connected (saved by Fritzing 0.9.3b)
breadboards: 2

parts:
  Raspberry_Pi_1 = Raspberry Pi 3 [part_number=RPI-3-V1.2]  # not connected
  IC1 = IC, DIP package, 40 pins [chip_label="GPIO Breakout"]
  Raspberry_Pi_2 = Raspberry Pi 3 [part_number=RPI-3-V1.2]  # not connected
  IC2 = IC, DIP package, 40 pins [chip_label="GPIO Breakout"]
  R1 = Resistor [tolerance=±5% resistance=220 package=THT]

nets:
  N1: IC1.pin25, R1.Pin_1
  N2: IC2.pin25, R1.Pin_0

notes:
  Pin 12
