# Fritzing sketch led_blink (saved by Fritzing 0.9.3b)
breadboards: 1

parts:
  LED1 = LED - 5mm [color="Green (555nm)" package="5 mm [THT]"]
  R1 = Resistor [tolerance=±5% resistance=220 package="2512 [SMD]"]
  Raspberry_Pi_1 = Raspberry Pi 3 [part_number=RPI-3-V1.2]  # not connected
  IC1 = IC, DIP package, 40 pins [chip_label="GPIO Breakout"]

nets:
  N1: LED1.cathode, R1.Pin_0
  N2: LED1.anode, IC1.pin6

notes:
  Pin 17
